# Fritzing sketch Piscine (saved by Fritzing 0.9.3b)
stripboards: 1

parts:
  Z-uno_2_1 = Z-Uno 2.0
  J1 = Screw terminal - 2 pins [package=THT]
  J2 = male pin header, 3 pins [form="♂ (male)"]
  R1 = Resistor [tolerance=±5% resistance=4.7k package=THT]
  R2 = Resistor [tolerance=±5% resistance=4.7k package=THT]
  J3 = male pin header, 3 pins [form="♂ (male)"]
  J4 = male pin header, 4 pins [form="♂ (male)"]
  J5 = male pin header, 3 pins [form="♂ (male)"]
  R3 = Resistor [tolerance=±1% resistance=3.3k package=THT]
  R4 = Resistor [tolerance=±1% resistance=3.3k package=THT]
  R5 = Resistor [tolerance=±1% resistance=2.2k package=THT]
  R6 = Resistor [tolerance=±1% resistance=2.2k package=THT]
  J6 = male pin header, 3 pins [form="♂ (male)"]
  Composant1 = LCD1602-I2C
  J7 = male pin header, 5 pins [form="♂ (male)"]
  U1 = Module 4 Relais 5V [package="Module 4 Relais 5V"]
  J8 = male pin header, 4 pins [form="♂ (male)"]
  J9 = male pin header, 2 pins [form="♂ (male)"]
  J10 = male pin header, 3 pins [form="♂ (male)"]
  J11 = screw terminal, 3 pins
  AMS7111-3_3 = Adafruit LM3671 Buck Converter [part_number=AMS7111-3.3]
  R7 = Rotary Potentiometer (Large) [maximum_resistance=10kΩ package=THT]
  R8 = Rotary Potentiometer (Large) [maximum_resistance=10kΩ package=THT]

nets:
  5V: Z-uno_2_1.5V, J1.pin1, J5.pin2, J6.pin2, Composant1.VCC, J7.pin4, U1.JD-VCC, J9.pin1, J10.pin1, AMS7111-3_3.VIN
  GND: Z-uno_2_1.GND#3, J1.pin2, J2.pin1, J3.pin1, J5.pin1, R3.Pin_0, R4.Pin_0, J6.pin1, Composant1.GND, J7.pin5, U1.GND, J9.pin2, J10.pin2, AMS7111-3_3.GND, R7.leg2, R8.leg2
  N1: Z-uno_2_1.3V3#4, J2.pin2, R1.Pin_1, R2.Pin_1, J3.pin2, J10.pin3, J11.pin1, J11.pin2, J11.pin3, R7.leg1, R8.leg1
  N2: Z-uno_2_1.pin3, R3.Pin_1, R5.Pin_0
  N3: Z-uno_2_1.pin4, R4.Pin_1, R6.Pin_0
  N4: Z-uno_2_1.pin5, R7.wiper
  N5: Z-uno_2_1.pin6, R8.wiper
  N6: Z-uno_2_1.pin8, Z-uno_2_1.ANT
  N7: Z-uno_2_1.ANT_U.FL, Z-uno_2_1.pin9, Composant1.SCL, J7.pin2
  N8: Z-uno_2_1.pin10, Composant1.SDA, J7.pin1
  N9: Z-uno_2_1.pin11, R2.Pin_0, J3.pin3
  N10: Z-uno_2_1.pin12, J2.pin3, R1.Pin_0
  N11: Z-uno_2_1.pin14, J8.pin4
  N12: Z-uno_2_1.pin15, J8.pin3
  N13: Z-uno_2_1.pin16, J8.pin2
  N14: Z-uno_2_1.pin_17, J8.pin1
  N15: Z-uno_2_1.pin_19, J4.pin4, U1.IN4
  N16: Z-uno_2_1.pin_20, J4.pin3, U1.IN3
  N17: Z-uno_2_1.pin_21, J4.pin2, U1.IN2
  N18: Z-uno_2_1.pin_22, Z-uno_2_1.3V3#44, J4.pin1, U1.IN1
  N19: Z-uno_2_1.pin_23, Z-uno_2_1.GND#43
  N20: J5.pin3, R5.Pin_1
  N21: R6.Pin_1, J6.pin3
  VCC: U1.VCC, AMS7111-3_3.3.3V

notes:
  Etalonnage ORP
  Etalonnage Ph
  Sonde ORP
  Sonde Ph
  Commande lumière
  Demande horaire
  Mode AUTO
  Mode MARCHE FORCEE
  Sonde T° Local
  Sonde T° Eau
  Eclairage
  Pompe
  Electrolyseur

custom parts:
  Z-Uno 2.0: The Teensy is a complete USB-based microcontoller development system, in a very small footprint, capable of implementing many types of projects. All programming is done via the USB port. No special programmer is needed, only a standard micro-USB cable and a PC or Macintosh with a USB port. It has a USB keyboard/mouse/joystick emulation stack and can be programmed through Arduino IDE. Z-Uno is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
  LCD1602-I2C: A standard character display, usually with 2x16 characters. Comes in many colors with LCM1602 IIC attached.
  Module 4 Relais 5V: Module 4 Relais 5V 4x SPD-06VDC-SD-C
  Adafruit LM3671 Buck Converter: Your power supply problems just got SUPER SOLVED! This 3.3V Buck Converter Breakout board is great for supplying power to low voltage circuits from a single Li-Ion cell battery or USB power. This chip provides up to 600-mA load current across the entire input voltage range of 3.5 to 5.5V. Great for your portable project, we made this "pin compatible" with the LM1117-3.3V TO-220 chip so you can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
